# Fritzing sketch Input - Distance (saved by Fritzing 0.9.1b)
breadboards: 1

parts:
  Part1 = Arduino Nano (Rev3.0)
  Part2 = SRF05 Ultrasonic Rangefinder

nets:
  GND: Part1.GND, Part2.GND
  N1: Part1.D12/MISO, Part2.Echo
  5V: Part1.5V, Part2.VCC
  N2: Part1.D13/SCK, Part2.Trig
