# Fritzing sketch Input - LDR (saved by Fritzing 0.9.1b)
breadboards: 1

parts:
  R2 = Resistor [tolerance=±5% resistance=1k package="0805 [SMD]"]
  R3 = Photocell (LDR) [package=THT]

nets:
  N1: R2.Pin_1, R3.pin_0
